// Logisim project cpu.circ as structural Verilog: 1 circuit, main circuit main
module main (
);

  wire button_1_out, clock_1_out, demultiplexer_1_out0, demultiplexer_1_out1, demultiplexer_1_out2,
       demultiplexer_1_out3;
  wire [7:0] adder_1_out, multiplexer_1_out, register_1_q, register_2_q, register_3_q, register_4_q,
       register_5_q, rom_1_data;

  ROM rom_1 (.addr(register_1_q), .data(rom_1_data));
  Clock clock_1 (.out(clock_1_out));
  LED led_1 (.in(clock_1_out));
  Register register_1 (.D(adder_1_out), .en(1'b1), .clk(clock_1_out), .Q(register_1_q), .clr(button_1_out));
  Button button_1 (.out(button_1_out));
  Adder adder_1 (.a(register_1_q), .b(8'h1), .out(adder_1_out), .cin(1'b0));  // open: cout
  TTY tty_1 (.data(rom_1_data[6:0]), .clk(clock_1_out), .we(1'b1), .clr(button_1_out));
  Register register_2 (.D(8'hc3), .en(demultiplexer_1_out0), .clk(clock_1_out), .Q(register_2_q), .clr(button_1_out));
  Demultiplexer #(.select(2), .enable("false")) demultiplexer_1 (
    .out0(demultiplexer_1_out0), .out1(demultiplexer_1_out1), .out2(demultiplexer_1_out2),
    .out3(demultiplexer_1_out3), .in(1'b1), .sel(2'b11));
  // Probe on 1'b1
  Register register_3 (.D(8'hc3), .en(demultiplexer_1_out1), .clk(clock_1_out), .Q(register_3_q), .clr(button_1_out));
  Register register_4 (.D(8'hc3), .en(demultiplexer_1_out2), .clk(clock_1_out), .Q(register_4_q), .clr(button_1_out));
  Multiplexer #(.select(2), .width(8), .enable("false")) multiplexer_1 (
    .in0(register_2_q), .in1(register_3_q), .in2(register_4_q), .in3(register_5_q), .out(multiplexer_1_out),
    .sel(2'b10));
  // Probe on multiplexer_1_out
  // Probe on 8'hc3
  Register register_5 (.D(8'hc3), .en(demultiplexer_1_out3), .clk(clock_1_out), .Q(register_5_q), .clr(button_1_out));

  // Notes on the sheet:
  //   contents of rom_1 (hex, n*v repeats v):
  //   6e 6f 6b 75 64 6f 20 63 75 72 69 6f 73 6f a
  //   RESET
  //   PC
  //   WRITE SELECT
  //   R0
  //   R1
  //   REG OUT
  //   R2
  //   REG IN
  //   R3
endmodule
